# Fritzing sketch FED Schematic (saved by Fritzing 0.9.2b)
breadboards: 1

parts:
  IC1 = L293D [package=THT]
  IR1 = TSOP312.., 314.. [package=THT]
  Part2 = Arduino Wireless SD Shield
  U1 = 7-SEGMENT-4DIGIT [package=7-segment-4digit]
  MOTOR1 = Adafruit Gear-Reduced Stepper Motor (small)

nets:
  N1: IC1.Enable_1, IC1.+Vmotor, IC1.Enable_2, IC1.+V, Part2.+5V, U1.7
  N2: IC1.In_1, Part2.D7
  N3: IC1.Out_1_(_Controlled_by_Enable_1_), MOTOR1.BLUE
  N4: IC1.0V, Part2.GND, U1.8
  N5: IC1.Out_2_(_Controlled_by_Enable_1_), MOTOR1.YELLOW
  N6: IC1.In_2, Part2.D6
  N7: IC1.In_3, Part2.D5
  N8: IC1.Out_3_(_Controlled_by_Enable_2_), MOTOR1.PINK
  N9: IC1.Out_4_(_Controlled_by_Enable_2_), MOTOR1.ORANGE
  N10: IC1.In_4, Part2.SD_CS
  N11: IR1.Data, Part2.D2
  N12: Part2.D3, U1.1

custom parts:
  Adafruit Gear-Reduced Stepper Motor (small): Adafruit gear-reduction stepper motor (small)
